# Fritzing sketch prototype_wiring (saved by Fritzing 1.0.8)
breadboards: 1

parts:
  Mod1 = Raspberry Pi 4B
  Adafruit_SCD-1 = Adafruit SCD-41
  D1 = LTE-302 [package=lte-302]
  R1 = Resistor [tolerance=±5% resistance=1kΩ power=0.25W package=THT]

nets:
  3V3: Mod1.3V3, Adafruit_SCD-1.VIN
  N1: Mod1.GPIO2, Adafruit_SCD-1.SDA
  N2: Mod1.GPIO3, Adafruit_SCD-1.SCL
  GND: Mod1.GND, Adafruit_SCD-1.GND, D1.C
  N3: Mod1.GPIO17, R1.Pin_0
  N4: D1.A, R1.Pin_1

custom parts:
  Adafruit SCD-41: Abstract connection-diagram part; not a mechanical footprint or simulation model.
